// Logisim project Circuito.circ as structural Verilog: 6 circuits, main circuit Circuito Principal
module Circuito_Principal (
  input  SET,
  input  CLK,
  input  RESET,
  input  [2:0] HORIZONTAL,
  input  [2:0] VERTICAL,
  output [3:0] LEFT_UP_DOWN_RIGHT
);

  wire MEMORIA_out_10, MEMORIA_out_11, MEMORIA_out_12, MEMORIA_out_13, MEMORIA_out_14, MEMORIA_out_15,
       or_1_out;
  wire [5:0] LOGICA_ESTADOS_s5, multiplexer_1_out;

  Multiplexer #(.width(6), .enable("false")) multiplexer_1 (
    .in0({HORIZONTAL, VERTICAL}), .in1(LOGICA_ESTADOS_s5), .out(multiplexer_1_out), .sel(or_1_out));
  or or_1 (or_1_out, LOGICA_ESTADOS_s5[0], LOGICA_ESTADOS_s5[1], LOGICA_ESTADOS_s5[2], LOGICA_ESTADOS_s5[3], LOGICA_ESTADOS_s5[4], LOGICA_ESTADOS_s5[5]);
  Memoria MEMORIA (
    .D(multiplexer_1_out[5]), .D_2(multiplexer_1_out[4]), .D_3(multiplexer_1_out[3]),
    .D_4(multiplexer_1_out[2]), .D_5(multiplexer_1_out[1]), .D_6(multiplexer_1_out[0]), .SET(SET), .CLK(CLK),
    .RESET(RESET), .out_10(MEMORIA_out_10), .out_11(MEMORIA_out_11), .out_12(MEMORIA_out_12),
    .out_13(MEMORIA_out_13), .out_14(MEMORIA_out_14), .out_15(MEMORIA_out_15));
  CC_ESTADOS LOGICA_ESTADOS (
    .H0(MEMORIA_out_10), .H1(MEMORIA_out_11), .H2(MEMORIA_out_12), .V0(MEMORIA_out_13), .V1(MEMORIA_out_14),
    .V2(MEMORIA_out_15), .S0(LOGICA_ESTADOS_s5[5]), .S1(LOGICA_ESTADOS_s5[4]), .S2(LOGICA_ESTADOS_s5[3]),
    .S3(LOGICA_ESTADOS_s5[2]), .S4(LOGICA_ESTADOS_s5[1]), .S5(LOGICA_ESTADOS_s5[0]));
  CC_SALIDA LOGICA_SALIDA (
    .S0(MEMORIA_out_10), .S1(MEMORIA_out_11), .S2(MEMORIA_out_12), .S3(MEMORIA_out_13), .S4(MEMORIA_out_14),
    .S5(MEMORIA_out_15), .out_7(LEFT_UP_DOWN_RIGHT));

  // Notes on the sheet:
  //   HORIZONTAL: pull=down
endmodule

module CC_ESTADOS (
  input  H0,
  input  H1,
  input  H2,
  input  V0,
  input  V1,
  input  V2,
  output S0,
  output S1,
  output S2,
  output S3,
  output S4,
  output S5
);

  wire and_1_out, and_2_out, and_3_out, and_4_out, and_5_out, and_6_out, and_7_out, and_8_out, and_9_out,
       and_10_out, and_11_out, and_12_out, and_13_out, and_14_out, and_15_out, and_16_out, and_17_out,
       and_18_out, and_19_out, and_20_out, and_21_out, and_22_out, and_23_out, and_24_out, and_25_out,
       and_26_out, and_27_out, and_28_out, and_29_out, and_30_out, and_31_out, and_32_out, and_33_out,
       and_34_out, and_35_out, not_1_out, not_2_out, not_3_out, not_4_out, not_5_out, not_6_out, not_7_out,
       not_8_out, not_9_out, not_10_out, not_11_out, not_12_out, not_13_out, not_14_out, not_15_out,
       not_16_out, not_17_out, not_18_out, not_19_out, not_20_out, not_21_out, not_22_out, not_23_out,
       not_24_out, not_25_out, not_26_out, not_27_out, not_28_out, not_29_out, not_30_out, not_31_out,
       not_32_out, not_33_out, not_34_out, not_35_out, not_36_out, not_37_out, not_38_out, not_39_out,
       not_40_out, not_41_out, not_42_out, not_43_out, not_44_out, not_45_out, not_46_out, not_47_out,
       not_48_out, not_49_out, not_50_out, not_51_out, not_52_out, not_53_out, not_54_out, not_55_out,
       not_56_out, not_57_out;

  not not_1 (not_1_out, V2);
  not not_2 (not_2_out, V1);
  not not_3 (not_3_out, V1);
  not not_4 (not_4_out, V2);
  not not_5 (not_5_out, H0);
  not not_6 (not_6_out, H1);
  not not_7 (not_7_out, H0);
  not not_8 (not_8_out, H2);
  not not_9 (not_9_out, V0);
  not not_10 (not_10_out, H0);
  not not_11 (not_11_out, H2);
  not not_12 (not_12_out, H1);
  not not_13 (not_13_out, V1);
  not not_14 (not_14_out, H2);
  not not_15 (not_15_out, V1);
  not not_16 (not_16_out, H0);
  not not_17 (not_17_out, H2);
  not not_18 (not_18_out, V0);
  not not_19 (not_19_out, H0);
  not not_20 (not_20_out, H1);
  not not_21 (not_21_out, V0);
  not not_22 (not_22_out, V0);
  not not_23 (not_23_out, H0);
  not not_24 (not_24_out, H2);
  not not_25 (not_25_out, V2);
  not not_26 (not_26_out, H1);
  not not_27 (not_27_out, H2);
  not not_28 (not_28_out, V1);
  not not_29 (not_29_out, H0);
  not not_30 (not_30_out, H1);
  not not_31 (not_31_out, V2);
  not not_32 (not_32_out, H2);
  not not_33 (not_33_out, V0);
  not not_34 (not_34_out, V0);
  not not_35 (not_35_out, V1);
  not not_36 (not_36_out, H2);
  not not_37 (not_37_out, V2);
  not not_38 (not_38_out, H0);
  not not_39 (not_39_out, H1);
  not not_40 (not_40_out, V0);
  not not_41 (not_41_out, H0);
  not not_42 (not_42_out, H1);
  not not_43 (not_43_out, H1);
  not not_44 (not_44_out, H2);
  not not_45 (not_45_out, V0);
  not not_46 (not_46_out, H0);
  not not_47 (not_47_out, H1);
  not not_48 (not_48_out, H1);
  not not_49 (not_49_out, V1);
  not not_50 (not_50_out, H0);
  not not_51 (not_51_out, H1);
  not not_52 (not_52_out, H0);
  not not_53 (not_53_out, V0);
  not not_54 (not_54_out, V1);
  not not_55 (not_55_out, H1);
  not not_56 (not_56_out, H2);
  not not_57 (not_57_out, V2);
  and and_1 (and_1_out, H2, V0, not_1_out);
  and and_2 (and_2_out, H1, H2, not_2_out);
  and and_3 (and_3_out, H0, not_3_out);
  and and_4 (and_4_out, H0, not_4_out);
  and and_5 (and_5_out, H0, V0);
  and and_6 (and_6_out, not_5_out, not_6_out, V2);
  and and_7 (and_7_out, not_7_out, not_8_out, V1);
  and and_8 (and_8_out, not_9_out, V1, V2);
  and and_9 (and_9_out, not_10_out, not_11_out, V0);
  and and_10 (and_10_out, not_12_out, H2, not_13_out);
  and and_11 (and_11_out, H1, not_14_out, not_15_out);
  and and_12 (and_12_out, H0, H1, H2);
  and and_13 (and_13_out, not_16_out, not_17_out, not_18_out, V2);
  and and_14 (and_14_out, not_19_out, not_20_out, not_21_out, V1);
  and and_15 (and_15_out, not_22_out, V1, V2);
  and and_16 (and_16_out, not_23_out, not_24_out, V0, not_25_out);
  and and_17 (and_17_out, not_26_out, not_27_out, V0, not_28_out, V2);
  and and_18 (and_18_out, not_29_out, not_30_out, H2, not_31_out);
  and and_19 (and_19_out, H1, not_32_out, not_33_out);
  and and_20 (and_20_out, H0, H1, not_34_out, not_35_out);
  and and_21 (and_21_out, H0, H1, not_36_out, V1);
  and and_22 (and_22_out, H0, H1, V0, not_37_out);
  and and_23 (and_23_out, not_38_out, H1, V1);
  and and_24 (and_24_out, not_39_out, V1, V2);
  and and_25 (and_25_out, H1, V0, V1);
  and and_26 (and_26_out, H0, not_40_out);
  and and_27 (and_27_out, not_41_out, not_42_out, V2);
  and and_28 (and_28_out, not_43_out, not_44_out, not_45_out, V1);
  and and_29 (and_29_out, not_46_out, not_47_out, V0);
  and and_30 (and_30_out, not_48_out, V0, not_49_out);
  and and_31 (and_31_out, not_50_out, not_51_out, H2);
  and and_32 (and_32_out, not_52_out, H1, not_53_out, not_54_out);
  and and_33 (and_33_out, H0, not_55_out, not_56_out, not_57_out);
  and and_34 (and_34_out, H0, H2, V0);
  and and_35 (and_35_out, H0, H1, V0, V1);
  or or_1 (S0, and_1_out, and_2_out, and_3_out, and_4_out, and_5_out);
  or or_2 (S1, and_6_out, and_7_out, and_8_out, and_9_out, and_10_out, and_11_out, and_12_out);
  or or_3 (S2, and_13_out, and_14_out, and_15_out, and_16_out, and_17_out, and_18_out, and_19_out, and_20_out, and_21_out, and_22_out);
  or or_4 (S3, V0, and_23_out);
  or or_5 (S4, and_24_out, and_25_out, and_26_out);
  or or_6 (S5, and_27_out, and_28_out, and_29_out, and_30_out, and_31_out, and_32_out, and_33_out, and_34_out, and_35_out);
endmodule

module CC_SALIDA (
  input  S0,
  input  S1,
  input  S2,
  input  S3,
  input  S4,
  input  S5,
  output [3:0] out_7
);

  wire and_1_out, and_2_out, and_3_out, and_4_out, and_5_out, and_6_out, and_7_out, and_8_out, and_9_out,
       and_10_out, and_11_out, and_12_out, and_13_out, and_14_out, and_15_out, and_16_out, and_17_out,
       and_18_out, and_19_out, and_20_out, and_21_out, and_22_out, and_23_out, and_24_out, not_1_out,
       not_2_out, not_3_out, not_4_out, not_5_out, not_6_out, not_7_out, not_8_out, not_9_out, not_10_out,
       not_11_out, not_12_out, not_13_out, not_14_out, not_15_out, not_16_out, not_17_out, not_18_out,
       not_19_out, not_20_out, not_21_out, not_22_out, not_23_out, not_24_out, not_25_out, not_26_out,
       not_27_out, not_28_out, not_29_out, not_30_out, not_31_out, not_32_out, not_33_out, not_34_out,
       not_35_out, not_36_out, not_37_out, not_38_out, not_39_out, not_40_out, not_41_out, not_42_out,
       not_43_out, not_44_out, not_45_out, not_46_out, not_47_out, not_48_out, not_49_out, not_50_out,
       not_51_out, not_52_out;

  not not_1 (not_1_out, S1);
  not not_2 (not_2_out, S3);
  not not_3 (not_3_out, S3);
  not not_4 (not_4_out, S5);
  not not_5 (not_5_out, S4);
  not not_6 (not_6_out, S5);
  not not_7 (not_7_out, S1);
  not not_8 (not_8_out, S0);
  not not_9 (not_9_out, S3);
  not not_10 (not_10_out, S4);
  not not_11 (not_11_out, S0);
  not not_12 (not_12_out, S1);
  not not_13 (not_13_out, S1);
  not not_14 (not_14_out, S4);
  not not_15 (not_15_out, S0);
  not not_16 (not_16_out, S3);
  not not_17 (not_17_out, S4);
  not not_18 (not_18_out, S0);
  not not_19 (not_19_out, S5);
  not not_20 (not_20_out, S4);
  not not_21 (not_21_out, S5);
  not not_22 (not_22_out, S0);
  not not_23 (not_23_out, S1);
  not not_24 (not_24_out, S5);
  not not_25 (not_25_out, S0);
  not not_26 (not_26_out, S1);
  not not_27 (not_27_out, S2);
  not not_28 (not_28_out, S0);
  not not_29 (not_29_out, S2);
  not not_30 (not_30_out, S1);
  not not_31 (not_31_out, S2);
  not not_32 (not_32_out, S1);
  not not_33 (not_33_out, S4);
  not not_34 (not_34_out, S5);
  not not_35 (not_35_out, S4);
  not not_36 (not_36_out, S4);
  not not_37 (not_37_out, S5);
  not not_38 (not_38_out, S1);
  not not_39 (not_39_out, S2);
  not not_40 (not_40_out, S3);
  not not_41 (not_41_out, S5);
  not not_42 (not_42_out, S1);
  not not_43 (not_43_out, S4);
  not not_44 (not_44_out, S5);
  not not_45 (not_45_out, S1);
  not not_46 (not_46_out, S4);
  not not_47 (not_47_out, S5);
  not not_48 (not_48_out, S0);
  not not_49 (not_49_out, S3);
  not not_50 (not_50_out, S3);
  not not_51 (not_51_out, S4);
  not not_52 (not_52_out, S5);
  and and_1 (and_1_out, not_1_out, not_2_out, S4, S5);
  and and_2 (and_2_out, S1, not_3_out, not_4_out);
  and and_3 (and_3_out, S0, S2, not_5_out, not_6_out);
  and and_4 (and_4_out, S0, not_7_out, S2, S4);
  and and_5 (and_5_out, S0, S1, S4, S5);
  and and_6 (and_6_out, not_8_out, not_9_out, not_10_out, S5);
  and and_7 (and_7_out, not_11_out, not_12_out, S3);
  and and_8 (and_8_out, not_13_out, S3, not_14_out, S5);
  and and_9 (and_9_out, not_15_out, S2, not_16_out, not_17_out);
  and and_10 (and_10_out, not_18_out, S1, not_19_out);
  and and_11 (and_11_out, S1, not_20_out, not_21_out);
  and and_12 (and_12_out, not_22_out, not_23_out, S4, not_24_out);
  and and_13 (and_13_out, not_25_out, not_26_out, not_27_out, S3);
  and and_14 (and_14_out, not_28_out, not_29_out, S3, S5);
  and and_15 (and_15_out, not_30_out, not_31_out, S3, S4);
  and and_16 (and_16_out, not_32_out, S2, not_33_out, not_34_out);
  and and_17 (and_17_out, S1, S3, not_35_out, S5);
  and and_18 (and_18_out, S0, S2, not_36_out, not_37_out);
  and and_19 (and_19_out, not_38_out, not_39_out, not_40_out, S4, not_41_out);
  and and_20 (and_20_out, not_42_out, S3, not_43_out, not_44_out);
  and and_21 (and_21_out, not_45_out, S2, not_46_out, not_47_out);
  and and_22 (and_22_out, not_48_out, S1, not_49_out, S4);
  and and_23 (and_23_out, S0, not_50_out, not_51_out);
  and and_24 (and_24_out, S0, S2, S3, not_52_out);
  or or_1 (out_7[3], and_1_out, and_2_out, and_3_out, and_4_out, and_5_out);
  or or_2 (out_7[0], and_6_out, and_7_out, and_8_out, and_9_out, and_10_out, and_11_out);
  or or_3 (out_7[2], and_12_out, and_13_out, and_14_out, and_15_out, and_16_out, and_17_out, and_18_out);
  or or_4 (out_7[1], and_19_out, and_20_out, and_21_out, and_22_out, and_23_out, and_24_out);
endmodule

module Flip_Flop_D (
  input  SET,
  input  D,
  input  CLK,
  input  RESET,
  output Q,
  output Q_prime
);

  wire nand_1_out, nand_2_out, nand_3_out, nand_4_out, nand_5_out, nand_6_out, not_1_out, not_2_out,
       not_3_out, not_4_out;

  not not_1 (not_1_out, SET);
  not not_2 (not_2_out, D);
  not not_3 (not_3_out, RESET);
  nand nand_1 (nand_1_out, D, CLK);
  nand nand_2 (nand_2_out, CLK, not_2_out);
  not not_4 (not_4_out, CLK);
  nand nand_3 (nand_3_out, not_1_out, nand_1_out, nand_4_out);
  nand nand_4 (nand_4_out, nand_3_out, nand_2_out, not_3_out);
  nand nand_5 (nand_5_out, nand_3_out, not_4_out);
  nand nand_6 (nand_6_out, not_4_out, nand_4_out);
  nand nand_7 (Q_prime, Q, nand_6_out, not_3_out);
  nand nand_8 (Q, not_1_out, nand_5_out, Q_prime);
endmodule

module Memoria (
  input  SET,
  input  CLK,
  input  RESET,
  input  D,
  input  D_2,
  input  D_3,
  input  D_4,
  input  D_5,
  input  D_6,
  output out_10,
  output out_11,
  output out_12,
  output out_13,
  output out_14,
  output out_15
);

  Flip_Flop_D flip_flop_d_1 (.SET(SET), .D(D), .CLK(CLK), .RESET(RESET), .Q(out_10));  // open: Q_prime
  Flip_Flop_D flip_flop_d_2 (.SET(SET), .D(D_2), .CLK(CLK), .RESET(RESET), .Q(out_11));  // open: Q_prime
  Flip_Flop_D flip_flop_d_3 (.SET(SET), .D(D_3), .CLK(CLK), .RESET(RESET), .Q(out_12));  // open: Q_prime
  Flip_Flop_D flip_flop_d_4 (.SET(SET), .D(D_4), .CLK(CLK), .RESET(RESET), .Q(out_13));  // open: Q_prime
  Flip_Flop_D flip_flop_d_5 (.SET(SET), .D(D_5), .CLK(CLK), .RESET(RESET), .Q(out_14));  // open: Q_prime
  Flip_Flop_D flip_flop_d_6 (.SET(SET), .D(D_6), .CLK(CLK), .RESET(RESET), .Q(out_15));  // open: Q_prime
endmodule

module BAKUP (
  input  [2:0] HORIZONTAL,
  input  [2:0] VERTICAL,
  output LEFT,
  output RIGHT,
  output UP,
  output DOWN
);

  wire cc_salida_1_p7, cc_salida_1_p8, cc_salida_1_p9, cc_salida_1_p10, clock_1_out, d_ff_1_q, d_ff_2_q,
       d_ff_3_q, d_ff_4_q, d_ff_5_q, d_ff_6_q, or_1_out;
  wire [5:0] cc_estados_1_s5, multiplexer_1_out;

  Multiplexer #(.width(6)) multiplexer_1 (
    .in0({HORIZONTAL, VERTICAL}), .in1(cc_estados_1_s5), .out(multiplexer_1_out), .sel(or_1_out));  // open: en
  or or_1 (or_1_out, cc_estados_1_s5[0], cc_estados_1_s5[1], cc_estados_1_s5[2], cc_estados_1_s5[3], cc_estados_1_s5[4], cc_estados_1_s5[5]);
  Clock clock_1 (.out(clock_1_out));
  D_Flip_Flop d_ff_1 (.clk(clock_1_out), .D(multiplexer_1_out[5]), .Q(d_ff_1_q));  // open: Qn, preset, en, reset
  D_Flip_Flop d_ff_2 (.clk(clock_1_out), .D(multiplexer_1_out[4]), .Q(d_ff_2_q));  // open: Qn, preset, en, reset
  D_Flip_Flop d_ff_3 (.clk(clock_1_out), .D(multiplexer_1_out[3]), .Q(d_ff_3_q));  // open: Qn, preset, en, reset
  D_Flip_Flop d_ff_4 (.clk(clock_1_out), .D(multiplexer_1_out[2]), .Q(d_ff_4_q));  // open: Qn, preset, en, reset
  D_Flip_Flop d_ff_5 (.clk(clock_1_out), .D(multiplexer_1_out[1]), .Q(d_ff_5_q));  // open: Qn, preset, en, reset
  D_Flip_Flop d_ff_6 (.clk(clock_1_out), .D(multiplexer_1_out[0]), .Q(d_ff_6_q));  // open: Qn, preset, en, reset
  CC_ESTADOS cc_estados_1 (
    .H0(d_ff_1_q), .H1(d_ff_2_q), .H2(d_ff_3_q), .V0(d_ff_4_q), .V1(d_ff_5_q), .V2(d_ff_6_q),
    .S0(cc_estados_1_s5[5]), .S1(cc_estados_1_s5[4]), .S2(cc_estados_1_s5[3]), .S3(cc_estados_1_s5[2]),
    .S4(cc_estados_1_s5[1]), .S5(cc_estados_1_s5[0]));
  // CC_SALIDA cc_salida_1: pin names not known; wires that end beside it: d_ff_1_q, d_ff_2_q, d_ff_3_q, d_ff_4_q, d_ff_5_q, d_ff_6_q, cc_salida_1_p7, cc_salida_1_p8, cc_salida_1_p9, cc_salida_1_p10

  // Notes on the sheet:
  //   HORIZONTAL: pull=down
endmodule
